# Fritzing sketch arduino-nrF24 (saved by Fritzing 0.9.2b)
breadboards: 2

parts:
  NRF24L3 = NRF24L01
  Composant2 = Arduino Nano (Rev3.0)
  R4 = PHOTOCELL [package=photocell-kit]
  T1 = LM35 Temperature Sensor [package="TO92 [THT]"]
  R5 = Resistor [tolerance=±5% resistance=2.2k package="0603 [SMD]"]

nets:
  VCC: NRF24L3.VCC, Composant2.3V3
  N1: NRF24L3.CSN, Composant2.D7
  N2: NRF24L3.MOSI, Composant2.D11/MOSI
  N3: NRF24L3.IRQ, Composant2.D2
  GND: NRF24L3.GND, Composant2.GND, T1.+Vs, T1.GND, R5.Pin_0
  N4: NRF24L3.CE, Composant2.D8
  N5: NRF24L3.SCK, Composant2.D13/SCK
  N6: NRF24L3.MISO, Composant2.D12/MISO
  N7: Composant2.5V, R4.P$1
  N8: Composant2.A1, R4.P$2, R5.Pin_1
  N9: Composant2.A0, T1.Vout

notes:
  GND = GND
  VCC = 3.3V
  CE = D8
  CSN = D7
  SCK = D13
  MOSI = D11
  MISO = D12
  IRQ = D2 (Not Connected?)
  Pin disponible:
  a2,a3,a4,a5,a6,a7
  d3,d4,d5,d6,d9,d10,
  Temperature: A1
  Lumiere: A2

custom parts:
  NRF24L01: NRF24L01 module
